# Fritzing sketch Untitled Sketch (saved by Fritzing 0.9.3b)
breadboards: 1

parts:
  V1 = DC Power [voltage=3.3V]
  C1 = Ceramic Capacitor [capacitance=0.1µF package="100 mil [THT, multilayer]"]
  R3 = Resistor [tolerance=±5% resistance=10k package=THT]
  R5 = Resistor [tolerance=±5% resistance=10k package=THT]
  R1 = Resistor [tolerance=±5% resistance=10k package=THT]
  R4 = Resistor [tolerance=±5% resistance=2.2k package=THT]
  JP1 = Header 2 [package=jst-2-smd-vert]
  DS1 = DS18B20 1-Wire Temperature Sensor [part_number=DS18B20]
  U1 = ESP8266 WiFi Module [part_number=ESP8266]

nets:
  VDD: V1.V+, C1.0, R3.Pin_1, R5.Pin_1, R1.Pin_1, R4.Pin_0, JP1.2, DS1.VDD, U1.VCC
  GND: C1.1, JP1.1, DS1.GND, U1.GND
  N1: R3.Pin_0, U1.GPIO_2
  N2: R5.Pin_0, U1.RST
  N3: R1.Pin_0, U1.CH_PD
  N4: R4.Pin_1, DS1.DQ, U1.GPIO_0

custom parts:
  ESP8266 WiFi Module: Generic WiFi Module based on the ESP8266 with onboard PCB antenna and UART communications
